// Logisim project problem2.circ as structural Verilog: 1 circuit, main circuit main
module main (
);

  wire button_1_out, d_ff_1_q, d_ff_1_qn;

  Button button_1 (.out(button_1_out));
  D_Flip_Flop d_ff_1 (.D(d_ff_1_qn), .clk(button_1_out), .Q(d_ff_1_q), .Qn(d_ff_1_qn));  // open: preset, reset
  LED led_1 (.in(d_ff_1_q));

  // Notes on the sheet:
  //   7474
endmodule
