// Logisim project Problem2Adder.circ as structural Verilog: 3 circuits, main circuit main
module main (
  input  [7:0] A,
  input  CarryIn,
  input  [7:0] B,
  output Overflow,
  output Bit8,
  output Bit7,
  output Bit6,
  output Bit5,
  output Bit4,
  output Bit3,
  output Bit2,
  output Bit1
);

  wire fulladder_2_cout, fulladder_3_cout, fulladder_4_cout, fulladder_5_cout, fulladder_6_cout,
       fulladder_7_cout, fulladder_8_cout, undriven, undriven_2, undriven_3, undriven_4, undriven_5,
       undriven_6, undriven_7, undriven_8;

  FullAdder fulladder_1 (.A(A[7]), .B(undriven_8), .Cin(fulladder_2_cout), .Cout(Overflow), .Sum(Bit8));
  FullAdder fulladder_2 (.A(A[6]), .B(undriven_7), .Cin(fulladder_3_cout), .Cout(fulladder_2_cout), .Sum(Bit7));
  FullAdder fulladder_3 (.A(A[5]), .B(undriven_6), .Cin(fulladder_4_cout), .Cout(fulladder_3_cout), .Sum(Bit6));
  FullAdder fulladder_4 (.A(A[4]), .B(undriven_5), .Cin(fulladder_5_cout), .Cout(fulladder_4_cout), .Sum(Bit5));
  FullAdder fulladder_5 (.A(A[3]), .B(undriven_4), .Cin(fulladder_6_cout), .Cout(fulladder_5_cout), .Sum(Bit4));
  FullAdder fulladder_6 (.A(A[2]), .B(undriven_3), .Cin(fulladder_7_cout), .Cout(fulladder_6_cout), .Sum(Bit3));
  FullAdder fulladder_7 (.A(A[1]), .B(undriven_2), .Cin(fulladder_8_cout), .Cout(fulladder_7_cout), .Sum(Bit2));
  FullAdder fulladder_8 (.A(A[0]), .B(undriven), .Cin(CarryIn), .Cout(fulladder_8_cout), .Sum(Bit1));
endmodule

module HalfAdder (
  input  A,
  input  B,
  output Cout,
  output Sum
);

  and and_1 (Cout, A, B);
  xor xor_1 (Sum, A, B);
endmodule

module FullAdder (
  input  A,
  input  B,
  input  Cin,
  output Cout,
  output Sum
);

  wire halfadder_1_cout, halfadder_1_sum, halfadder_2_cout;

  HalfAdder halfadder_1 (.A(A), .B(B), .Cout(halfadder_1_cout), .Sum(halfadder_1_sum));
  HalfAdder halfadder_2 (.A(halfadder_1_sum), .B(Cin), .Cout(halfadder_2_cout), .Sum(Sum));
  or or_1 (Cout, halfadder_1_cout, halfadder_2_cout);
endmodule
